# Fritzing sketch car (saved by Fritzing 0.9.3b)
breadboards: 1

parts:
  부품2 = Bluetooth HC-05 Macho
  HG7881_Motor_Driver_Module1 = HG7881 Dual Channel Motor Driver Module
  HG7881_Motor_Driver_Module2 = HG7881 Dual Channel Motor Driver Module
  부품3 = Arduino Uno (Rev3)
  S1 = Toggle Switch [package=THT]
  M1 = Getriebemotor
  M2 = Getriebemotor
  M3 = Getriebemotor
  M4 = Getriebemotor
  VCC1 = 4 x AA Battery Box

nets:
  N1: 부품2.TXD, 부품3.D9_PWM
  N2: 부품2.RXD, 부품3.D8
  VCC: 부품2.VCC, HG7881_Motor_Driver_Module1.VCC, HG7881_Motor_Driver_Module2.VCC, 부품3.VIN, S1.L2
  GND: 부품2.GND, HG7881_Motor_Driver_Module1.GND, HG7881_Motor_Driver_Module2.GND, 부품3.GND, VCC1.-
  N3: HG7881_Motor_Driver_Module1.A-IB, HG7881_Motor_Driver_Module2.A-IB, 부품3.D5_PWM
  N4: HG7881_Motor_Driver_Module1.A-IA, HG7881_Motor_Driver_Module2.A-IA, 부품3.D4
  N5: HG7881_Motor_Driver_Module1.B-IB, HG7881_Motor_Driver_Module2.B-IB, 부품3.D3_PWM
  N6: HG7881_Motor_Driver_Module1.B-IA, HG7881_Motor_Driver_Module2.B-IA, 부품3.D2
  N7: HG7881_Motor_Driver_Module1.Motor_A_+, M2.pin_1
  N8: HG7881_Motor_Driver_Module1.Motor_A_-, M2.pin_2
  N9: HG7881_Motor_Driver_Module1.Motor_B_+, M1.pin_1
  N10: HG7881_Motor_Driver_Module1.Motor_B_-, M1.pin_2
  N11: HG7881_Motor_Driver_Module2.Motor_A_-, M3.pin_1
  N12: HG7881_Motor_Driver_Module2.Motor_B_+, M4.pin_2
  N13: HG7881_Motor_Driver_Module2.Motor_B_-, M4.pin_1
  N14: S1.COM, VCC1.+

custom parts:
  HG7881 Dual Channel Motor Driver Module: The HG7881 dual channel motor driver module is able to drive two DC motors. The supported voltage range is 2.5V to 12V.
  4 x AA Battery Box: A 4 x AA battery box.
