# Fritzing sketch controller (saved by Fritzing 0.9.3b)
breadboards: 2

parts:
  부품1 = Arduino Nano (Rev3.0) (ICSP)
  부품2 = Bluetooth HC-05 Macho
  R1 = Resistor [tolerance=±5% resistance=1k package="0805 [SMD]"]
  R2 = Resistor [tolerance=±5% resistance=1k package="0805 [SMD]"]
  U1 = LIPO-110mAh [package=lipo-110]
  TP1 = TP4056 [chip_label=TP4056 package="DIP (Dual Inline) [THT]"]
  S1 = Toggle Switch [package=THT]
  부품3 = Thumb Joystick
  S2 = Round Pushbutton
  S3 = Round Pushbutton

nets:
  GND: 부품1.GND, 부품2.GND, R1.Pin_1, R2.Pin_1, S1.L1, 부품3.GND
  N1: 부품1.D3, R2.Pin_0, S3.leg1
  N2: 부품1.D4, R1.Pin_0, S2.leg1
  N3: 부품1.D8, 부품2.RXD
  N4: 부품1.D9, 부품2.TXD
  VIN: 부품1.VIN, 부품2.VCC, TP1.pin3, S2.leg0, S3.leg0
  5V: 부품1.5V, 부품3.VCC
  N5: 부품1.A2, 부품3.SEL
  N6: 부품1.A1, 부품3.HORZ
  N7: 부품1.A0, 부품3.VERT
  N8: U1.+, TP1.pin4
  N9: U1.-, TP1.pin5
  N10: TP1.pin6, S1.COM

custom parts:
  TP4056: A DIP stand-in part for whatever IC you want. With 6 pins on a 300mil dual inline package (DIP) footprint.
